# Fritzing sketch plant_feeder (saved by Fritzing 0.9.3b)
breadboards: 1

parts:
  Distance_Sensor = hc-sr04
  Part3 = Soil Moisture Sensor
  U1 = LCD-16X2 [package=lcd-16x2]  # not connected
  Part2 = blueIOT RevB
  Part4 = Arduino Uno (Rev3) - ICSP
  RHT1 = Humidity and Temperature Sensor RHT03
  U3 = ESP8266 WiFi Module [part_number=ESP8266]
  Relay = G3VM-61E1 [package=g3vm-61e1]
  R1 = Resistor [tolerance=±5% resistance=1k package="0805 [SMD]"]
  R2 = Resistor [tolerance=±5% resistance=2.2k package="0805 [SMD]"]
  R3 = Resistor [tolerance=±5% resistance=10k package="0805 [SMD]"]
  R4 = Resistor [tolerance=±5% resistance=10k package="0805 [SMD]"]
  R5 = Resistor [tolerance=±5% resistance=10k package="0805 [SMD]"]
  S1 = Pushbutton [package="[SMD]"]
  S2 = Pushbutton [package="[SMD]"]
  LED1 = smd LED [color="Red (633nm)" package="1206 [SMD]"]
  R6 = Resistor [tolerance=±5% resistance=220 package="0805 [SMD]"]
  VCC1 = Battery block 9V
  M1 = DC Motor

nets (from the schematic view):
  VCC: Distance_Sensor.VCC, Part3.VCC, Part2.3V3, Part4.5V, RHT1.Vcc, Relay.P$3, R3.Pin_0, S1.Pin_3, S1.Pin_4, S2.Pin_3, S2.Pin_4
  GND: Distance_Sensor.Trig, Part3.GND, Part2.GND, Part4.D3_PWM, RHT1.GND_1
  N1: Distance_Sensor.Echo, Part4.D2
  GND_2: Distance_Sensor.GND, Part4.GND, U3.GND, Relay.P$2, R1.Pin_1, R4.Pin_1
  N2: Part3.SIG, Part4.A0
  N3: Part2.SCL/A5, Part4.A5/SCL
  N4: Part2.SCA/A4, Part4.A4/SDA
  N5: Part4.ICSP_MOSI, Part4.D11_PWM/MOSI, R5.Pin_1, LED1.cathode
  N6: Part4.D8, U3.TXD
  N7: Part4.D9_PWM, R2.Pin_1
  N8: Part4.D10_PWM/SS, R4.Pin_0, S1.Pin_1, S1.Pin_2
  N9: Part4.D12/MISO, R6.Pin_1
  N10: Part4.D5_PWM, RHT1.Data-signal, R3.Pin_1
  N11: Part4.D6_PWM, Relay.P$1
  3V3: Part4.3V3, U3.VCC, U3.CH_PD, U3.REST
  N12: U3.RXD, R1.Pin_0, R2.Pin_0
  N13: Relay.P$5, VCC1.+
  N14: Relay.P$6, M1.pin_2
  N15: R5.Pin_0, S2.Pin_1, S2.Pin_2
  N16: LED1.anode, R6.Pin_0
